# Fritzing sketch HC06 (saved by Fritzing 0.9.3b)
breadboards: 1

parts:
  BT1 = Bluetooth HC-06d [package=THT]
  Part1 = Arduino Uno (Rev3) - ICSP

nets:
  VCC: BT1.VCC, Part1.5V
  GND: BT1.GND, Part1.GND
  N1: BT1.TXD, Part1.D3_PWM
  N2: BT1.RXD, Part1.D4

custom parts:
  Bluetooth HC-06d: Bluetooth HC-06 - face down, pins down 16.5mm x 37.5mm PCB
