# Fritzing sketch HC06_LED_Motor (saved by Fritzing 0.9.3b)
breadboards: 1

parts:
  BT1 = Bluetooth HC-06d [package=THT]
  Part1 = Arduino Uno (Rev3) - ICSP
  LED1 = LED - 5mm [color="Red (633nm)" package="5 mm [THT]"]
  S1 = H-Bridge with L298N
  M1 = DC Motor
  BAT1 = Battery Holders [package=lipo-1100mAh]

nets:
  VCC: BT1.VCC, Part1.5V
  GND: BT1.GND, Part1.GND, LED1.cathode
  N1: BT1.TXD, Part1.D3_PWM
  N2: BT1.RXD, Part1.D4
  N3: Part1.D8, S1.IN2
  N4: Part1.D13/SCK, LED1.anode
  N5: Part1.D6_PWM, S1.ENA
  N6: Part1.D7, S1.IN1
  N7: S1.12V, BAT1.+
  N8: S1.GND, BAT1.-
  N9: S1.M1-01, M1.pin_2
  N10: S1.M1-02, M1.pin_1

custom parts:
  Bluetooth HC-06d: Bluetooth HC-06 - face down, pins down 16.5mm x 37.5mm PCB
  H-Bridge with L298N: h-bridge
