# Fritzing sketch HC06_LED_Servo (saved by Fritzing 0.9.3b)
breadboards: 1

parts:
  BT1 = Bluetooth HC-06d [package=THT]
  Part1 = Arduino Uno (Rev3) - ICSP
  LED1 = LED - 5mm [color="Red (633nm)" package="5 mm [THT]"]
  J1 = Basic Servo

nets:
  VCC: BT1.VCC, Part1.5V, J1.vcc
  GND: BT1.GND, Part1.GND, LED1.cathode, J1.gnd
  N1: BT1.TXD, Part1.D3_PWM
  N2: BT1.RXD, Part1.D4
  N3: Part1.D9_PWM, J1.pulse
  N4: Part1.D13/SCK, LED1.anode

custom parts:
  Bluetooth HC-06d: Bluetooth HC-06 - face down, pins down 16.5mm x 37.5mm PCB
